// Digital circuit D-70-submission1_AUTOMATIC.dig as structural Verilog
module D_70_submission1_AUTOMATIC (
  input  clk,
  input  RST,
  input  \input ,
  input  CE,
  output \sequence 
);

  wire and_1_out, comparator_1_gt, counter_1_ovf, multiplexer_1_out, not_1_out, reg_rst_ce_1_p4,
       reg_rst_ce_1_p5, S1_p5, S2_p5, S3_p5, S4_p5, S5_p5, S6_p5, S7_p5, xor_1_out, xor_2_out, xor_3_out,
       xor_4_out, xor_5_out;
  wire [3:0] counter_1_out;

  Comparator #(.Bits(4)) comparator_1 (.a(4'b1000), .b(counter_1_out), .gt(comparator_1_gt));  // open: eq, lt
  Counter #(.Bits(4)) counter_1 (.en(CE), .C(clk), .clr(RST), .out(counter_1_out), .ovf(counter_1_ovf));
  // REG_RST_CE reg_rst_ce_1: pin names not known; wires that end beside it: counter_1_ovf, clk, RST, reg_rst_ce_1_p4, reg_rst_ce_1_p5
  or or_1 (reg_rst_ce_1_p4, RST, not_1_out);
  Multiplexer multiplexer_1 (.sel(and_1_out), .in_0(xor_1_out), .in_1(\input ), .out(multiplexer_1_out));
  and and_1 (and_1_out, comparator_1_gt, not_1_out);
  not not_1 (not_1_out, reg_rst_ce_1_p5);
  // REG_RST_CE S7: pin names not known; wires that end beside it: multiplexer_1_out, clk, RST, CE, S7_p5
  xor xor_1 (xor_1_out, S7_p5, xor_2_out);
  // REG_RST_CE S6: pin names not known; wires that end beside it: S7_p5, clk, RST, CE, S6_p5
  xor xor_2 (xor_2_out, S6_p5, xor_3_out);
  // REG_RST_CE S5: pin names not known; wires that end beside it: S6_p5, clk, RST, CE, S5_p5
  xor xor_3 (xor_3_out, S5_p5, xor_4_out);
  // REG_RST_CE S4: pin names not known; wires that end beside it: S5_p5, clk, RST, CE, S4_p5
  // REG_RST_CE S3: pin names not known; wires that end beside it: S4_p5, clk, RST, CE, S3_p5
  // REG_RST_CE S2: pin names not known; wires that end beside it: S3_p5, clk, RST, CE, S2_p5
  xor xor_4 (xor_4_out, S2_p5, xor_5_out);
  // REG_RST_CE S1: pin names not known; wires that end beside it: S2_p5, clk, RST, CE, S1_p5
  xor xor_5 (xor_5_out, S1_p5, \sequence );
  // REG_RST_CE S0: pin names not known; wires that end beside it: S1_p5, clk, RST, CE, \sequence 
endmodule

/* Test case experiment1:
clk input RST sequence CE
0 0  1 0 1
C 0  1 0 1
#RESET, now values are known, start init. values
C 1  0 0 1
C 0  0 0 1
C 0  0 0 1
C 0  0 0 1
C 0  0 0 1
C 0  0 0 1
C 0  0 0 1
C 0  0 1 1	#initial values loaded, state 0
C 0  0 0 1
C 0  0 0 1
C 0  0 0 1
C 0  0 0 1
C 0  0 0 1
C 0  0 0 1
C 0  0 0 1
C 0  0 1 1
C 0  0 1 1
C 0  0 0 1
C 0  0 0 1
C 0  0 1 1
C 0  0 1 1
C 0  0 1 1
*/

/* Test case experiment2:
clk input RST sequence CE
0 0  1 0 1
C 0  1 0 1
#RESET, now values are known, start init. values
C 1  0 0 1
C 0  0 0 1
C 0  0 0 1
C 1  0 0 1
C 0  0 0 1
C 0  0 0 1
C 1  0 0 1
#start
C 0  0 1 1	#initial values loaded, state 0
C 0  0 0 1
C 0  0 0 1
C 0  0 1 1
C 0  0 0 1
C 0  0 0 1
C 0  0 1 1
C 0  0 0 1	#state 7
C 0  0 0 0	#start 5 idle cycles
C 0  0 0 0
C 0  0 0 0
C 0  0 0 0
C 0  0 0 0	#end idle cycles, reload
C 0  1 0 1
C 0  1 0 1
#RESET, now values are known, start init. values
C 1  0 0 1
C 0  0 0 1
C 0  0 0 1
C 0  0 0 1
C 0  0 0 1
C 0  0 0 1
C 0  0 0 1
C 0  0 1 1	#initial values loaded, state 0
C 0  0 0 1
C 0  0 0 1
C 0  0 0 1
C 0  0 0 1
*/
